# Fritzing sketch ESP32C3SM_LD2410 (saved by Fritzing 1.0.4)
circuit board: 4.29836cm x 4.64726cm
breadboards: 1

parts:
  Esp32c3_SuperMini = Esp32-c3 super mini
  HLK-PM1 = HLK-PM01
  AC = Screw terminal - 2 pins [package=THT]
  HLK-LD2410C = Hi-link HLK-LD2410C

nets:
  N1: Esp32c3_SuperMini.Pin_7, HLK-LD2410C.Pin_2
  N2: Esp32c3_SuperMini.Pin_8, HLK-LD2410C.Pin_1
  N3: Esp32c3_SuperMini.Pin_15, HLK-PM1.-Vo, HLK-LD2410C.Pin_4
  N4: Esp32c3_SuperMini.Pin_16, HLK-PM1.+Vo, HLK-LD2410C.Pin_5
  N5: HLK-PM1.AC#0, AC.pin2
  N6: HLK-PM1.AC#1, AC.pin1

custom parts:
  Esp32-c3 super mini: ESP32-C3 Development Board ESP32 SuperMini Development Board ESP32 Development Board WiFi Bluetooth.
  Hi-link HLK-LD2410C: LD2410C is a high-sensitivity 24GHz human presence status sensing module. bb reversed for on perfboard in breadboard.
