# Fritzing sketch ESP32C3SM_LD2420 (saved by Fritzing 1.0.4)
circuit board: 4.29836cm x 4.64726cm
breadboards: 1

parts:
  Esp32c3_Super_Mini = Esp32-c3 super mini
  HLK-LD2420 = HLK-LD2420
  HLK-PM1 = HLK-PM01
  AC = Screw terminal - 2 pins [package=THT]

nets:
  N1: Esp32c3_Super_Mini.Pin_7, HLK-LD2420.Pin_4
  N2: Esp32c3_Super_Mini.Pin_8, HLK-LD2420.Pin_3
  N3: Esp32c3_Super_Mini.Pin_14, HLK-LD2420.Pin_1
  N4: Esp32c3_Super_Mini.Pin_15, HLK-LD2420.Pin_2, HLK-PM1.-Vo
  N5: Esp32c3_Super_Mini.Pin_16, HLK-PM1.+Vo
  N6: HLK-PM1.AC#0, AC.pin2
  N7: HLK-PM1.AC#1, AC.pin1

custom parts:
  Esp32-c3 super mini: ESP32-C3 Development Board ESP32 SuperMini Development Board ESP32 Development Board WiFi Bluetooth.
  HLK-LD2420: HLK-LD2420 is mainly used to detect whether there is movement or slight movement of the human body in the indoor scene perception area.
